// Logisim project s-mips.circ as structural Verilog
module S_MIPS_Board (
  input  DESHABILITAR_DISPATCHER,
  output halt
);

  wire button_1_out, CLK, CS, d_ff_1_q, LCLR, LoadRAM, LoadRAMOn, LW, R_R_W, R_W, ram_dispatcher_1_finished,
       RCS, Reset_out, RST, TTY_EN;
  wire [2:0] KDB;
  wire [3:0] LMask, Mask, ram_1_read_time, RMask, s_mips_1_mask;
  wire [6:0] KDB_DATA, TTY_DATA;
  wire [15:0] Addr, LAddr, RAddr;
  wire [31:0] I0, I1, I2, I3, LData, ram_1_data_out_0, ram_1_data_out_1, ram_1_data_out_2, ram_1_data_out_3,
       RI0, RI1, RI2, RI3;

  TTY #(.rows(25), .cols(80)) tty_1 (.data(TTY_DATA), .clk(CLK), .we(TTY_EN), .clr(RST));
  not not_1 (LoadRAMOn, ram_dispatcher_1_finished);
  RAM_Dispatcher ram_dispatcher_1 (
    .WriteTime(ram_1_read_time), .Clock(CLK), .Data(LData), .Address(LAddr), .Mask(LMask),
    .Finished(ram_dispatcher_1_finished), .Write(LW), .CLR(LCLR));
  Keyboard #(.buflen(64)) keyboard_1 (.clk(CLK), .re(KDB[0]), .avail(KDB[2]), .data(KDB_DATA));  // open: clr
  RAM ram_1 (
    .Address(RAddr), .Data_Out_0(ram_1_data_out_0), .Data_Out_1(ram_1_data_out_1),
    .Data_Out_2(ram_1_data_out_2), .Data_Out_3(ram_1_data_out_3), .Data_In_0(RI0), .Data_In_1(RI1),
    .Data_In_2(RI2), .Data_In_3(RI3), .Mask(RMask), .nRead_Write(R_R_W), .Chip_Select(RCS),
    .Read_Time(ram_1_read_time), .Reset(button_1_out), .Write_Time(ram_1_read_time));
  Button button_1 (.out(button_1_out));
  D_Flip_Flop d_ff_1 (.clk(CLK), .D(1'b1), .Q(d_ff_1_q), .reset(Reset_out));  // open: Qn, preset, en
  Button Reset (.out(Reset_out));
  S_MIPS s_mips_1 (
    .Kbd_Enable(KDB[0]), .Address(Addr), .Kbd_Clear(KDB[1]), .Kbd_Available(KDB[2]),
    .Kbd_ASCII_Data(KDB_DATA), .TTY_Enable(TTY_EN), .TTY_ASCII_Data(TTY_DATA), .Reset(RST), .Stop(halt),
    .RAM_In_1(I1), .RAM_In_3(I3), .Mask(s_mips_1_mask), .Read_Time(ram_1_read_time),
    .Write_Time(ram_1_read_time), .nRead_Write(R_W), .Chip_Select(CS));  // open: RAM_Out_0, RAM_Out_1, RAM_Out_2, RAM_Out_3, RAM_In_0, RAM_In_2
  D_Flip_Flop d_ff_2 (.clk(CLK), .D(d_ff_1_q), .Qn(LCLR), .reset(Reset_out));  // open: Q, preset, en
  or or_1 (RST, LCLR, LoadRAM);
  Clock clock_1 (.out(CLK));
  Multiplexer #(.width(32), .enable("false")) multiplexer_1 (.in0(I0), .in1(LData), .out(RI0), .sel(LoadRAM));
  Multiplexer #(.width(32), .enable("false")) multiplexer_2 (.in0(I1), .in1(LData), .out(RI1), .sel(LoadRAM));
  Multiplexer #(.width(32), .enable("false")) multiplexer_3 (.in0(I2), .in1(LData), .out(RI2), .sel(LoadRAM));
  Multiplexer #(.width(32), .enable("false")) multiplexer_4 (.in0(I3), .in1(LData), .out(RI3), .sel(LoadRAM));
  and and_1 (LoadRAM, ~DESHABILITAR_DISPATCHER, LoadRAMOn);  // AND_Gate
  Multiplexer #(.width(16), .enable("false")) multiplexer_5 (.in0(Addr), .in1(LAddr), .out(RAddr), .sel(LoadRAM));
  Multiplexer #(.width(4), .enable("false")) multiplexer_6 (.in0(Mask), .in1(LMask), .out(RMask), .sel(LoadRAM));
  Multiplexer #(.enable("false")) multiplexer_7 (.in0(CS), .in1(LW), .out(RCS), .sel(LoadRAM));
  Multiplexer #(.enable("false")) multiplexer_8 (.in0(R_W), .in1(LW), .out(R_R_W), .sel(LoadRAM));

  // Notes on the sheet:
  //   NO MODIFICAR
  //   Keyboard
endmodule

module RAM (
  input  [15:0] Address,
  input  [31:0] Data_In_0,
  input  [31:0] Data_In_1,
  input  [31:0] Data_In_2,
  input  [31:0] Data_In_3,
  input  [3:0] Mask,
  input  nRead_Write,
  input  Chip_Select,
  input  Reset,
  output [31:0] Data_Out_0,
  output [31:0] Data_Out_1,
  output [31:0] Data_Out_2,
  output [31:0] Data_Out_3,
  output [3:0] Read_Time,
  output [3:0] Write_Time
);

  wire and_2_out, and_3_out, and_4_out, and_5_out, and_6_out, and_7_out, and_8_out, and_9_out, Changed, CLK,
       comparator_2_eq, comparator_3_eq, comparator_4_eq, comparator_5_eq, comparator_6_eq, Count,
       demultiplexer_3_out0, Idle, Idle_q, Load, Load0, Load1, nand_1_out, or_1_out, or_2_out, or_3_out,
       or_4_out, or_5_out, or_6_out, or_7_out, or_8_out, or_9_out, or_10_out, Proc_q, Update_Mem, Zero_Time;
  wire [3:0] counter_1_q, multiplexer_1_out, subtractor_1_out;
  wire [31:0] register_1_q, register_2_q, register_3_q, register_4_q, register_5_q;

  // Probe on 4'b0011
  // Probe on 4'b0010
  Multiplexer #(.width(4), .enable("false")) multiplexer_1 (
    .in0(4'b0011), .in1(4'b0010), .out(multiplexer_1_out), .sel(nRead_Write));
  or or_1 (or_1_out, Idle, Update_Mem);
  or or_2 (or_2_out, ~Chip_Select, Reset);  // OR_Gate
  Subtractor #(.width(4)) subtractor_1 (.a(multiplexer_1_out), .b(4'b0010), .out(subtractor_1_out));  // open: bin, bout
  D_Flip_Flop u_Idle (.clk(CLK), .D(or_1_out), .Q(Idle_q), .preset(or_2_out));  // open: Qn, en, reset
  Demultiplexer #(.enable("false")) demultiplexer_1 (.out0(Idle), .out1(Load0), .in(Idle_q), .sel(Changed));
  // Probe on counter_1_q
  Counter #(.width(4), .max('hf)) counter_1 (
    .load(Load), .D(subtractor_1_out), .count(Count), .Q(counter_1_q), .clk(CLK), .clr(or_3_out));  // open: carry
  or or_3 (or_3_out, ~Chip_Select, Reset);  // OR_Gate
  Comparator #(.width(4), .mode("unsigned")) comparator_1 (
    .a(4'b0000), .b(counter_1_q), .eq(Zero_Time));  // open: gt, lt
  or or_4 (or_4_out, Count, Load0, Load1);
  Register #(.width(32)) register_1 (.D(Data_In_0), .en(Chip_Select), .Q(register_1_q), .clk(CLK), .clr(or_5_out));
  or or_5 (or_5_out, ~Chip_Select, Reset);  // OR_Gate
  Register #(.width(32)) register_2 (.D(Data_In_1), .en(Chip_Select), .Q(register_2_q), .clk(CLK), .clr(or_6_out));
  or or_6 (or_6_out, ~Chip_Select, Reset);  // OR_Gate
  Register #(.width(32)) register_3 (.D(Data_In_2), .en(Chip_Select), .Q(register_3_q), .clk(CLK), .clr(or_7_out));
  or or_7 (or_7_out, ~Chip_Select, Reset);  // OR_Gate
  Register #(.width(32)) register_4 (.D(Data_In_3), .en(Chip_Select), .Q(register_4_q), .clk(CLK), .clr(or_8_out));
  or or_8 (or_8_out, ~Chip_Select, Reset);  // OR_Gate
  Register #(.width(32)) register_5 (
    .D({{11{1'b1}}, nRead_Write, Mask, Address}), .en(Chip_Select), .Q(register_5_q), .clk(CLK),
    .clr(or_9_out));
  or or_9 (or_9_out, ~Chip_Select, Reset);  // OR_Gate
  D_Flip_Flop Proc (.clk(CLK), .D(or_4_out), .Q(Proc_q), .reset(or_10_out));  // open: Qn, preset, en
  or or_10 (or_10_out, ~Chip_Select, Reset);  // OR_Gate
  Demultiplexer #(.enable("false")) demultiplexer_2 (
    .out0(Count), .out1(Update_Mem), .in(demultiplexer_3_out0), .sel(Zero_Time));
  Demultiplexer #(.enable("false")) demultiplexer_3 (
    .out0(demultiplexer_3_out0), .out1(Load1), .in(Proc_q), .sel(Changed));
  Clock clock_1 (.out(CLK));
  Comparator #(.width(32)) comparator_2 (.a(register_1_q), .b(Data_In_0), .eq(comparator_2_eq));  // open: gt, lt
  Comparator #(.width(32)) comparator_3 (.a(register_2_q), .b(Data_In_1), .eq(comparator_3_eq));  // open: gt, lt
  Comparator #(.width(32)) comparator_4 (.a(register_3_q), .b(Data_In_2), .eq(comparator_4_eq));  // open: gt, lt
  Comparator #(.width(32)) comparator_5 (.a(register_4_q), .b(Data_In_3), .eq(comparator_5_eq));  // open: gt, lt
  Comparator #(.width(32)) comparator_6 (
    .a(register_5_q), .b({{11{1'b1}}, nRead_Write, Mask, Address}), .eq(comparator_6_eq));  // open: gt, lt
  nand nand_1 (nand_1_out, comparator_6_eq, comparator_2_eq, comparator_3_eq, comparator_4_eq, comparator_5_eq);
  and and_1 (Changed, nand_1_out, Chip_Select);
  or or_11 (Load, Count, Load1, Load0);
  and and_2 (and_2_out, Mask[0], Update_Mem, nRead_Write);
  and and_3 (and_3_out, Mask[1], Update_Mem, nRead_Write);
  and and_4 (and_4_out, Mask[2], Update_Mem, nRead_Write);
  and and_5 (and_5_out, Mask[3], Update_Mem, nRead_Write);
  RAM_part #(.addrWidth(16), .dataWidth(32), .bus("separate")) ram_1 (
    .addr(Address), .din(Data_In_0), .data(Data_Out_0), .str(and_2_out), .sel(Chip_Select), .clk(CLK),
    .ld(and_6_out), .clr(Reset));
  and and_6 (and_6_out, ~nRead_Write, Idle);  // AND_Gate
  RAM_part #(.addrWidth(16), .dataWidth(32), .bus("separate")) ram_2 (
    .addr(Address), .din(Data_In_1), .data(Data_Out_1), .str(and_3_out), .sel(Chip_Select), .clk(CLK),
    .ld(and_7_out), .clr(Reset));
  and and_7 (and_7_out, ~nRead_Write, Idle);  // AND_Gate
  RAM_part #(.addrWidth(16), .dataWidth(32), .bus("separate")) ram_3 (
    .addr(Address), .din(Data_In_2), .data(Data_Out_2), .str(and_4_out), .sel(Chip_Select), .clk(CLK),
    .ld(and_8_out), .clr(Reset));
  and and_8 (and_8_out, ~nRead_Write, Idle);  // AND_Gate
  RAM_part #(.addrWidth(16), .dataWidth(32), .bus("separate")) ram_4 (
    .addr(Address), .din(Data_In_3), .data(Data_Out_3), .str(and_5_out), .sel(Chip_Select), .clk(CLK),
    .ld(and_9_out), .clr(Reset));
  and and_9 (and_9_out, ~nRead_Write, Idle);  // AND_Gate

  assign Read_Time = 4'b0011;
  assign Write_Time = 4'b0010;

  // Other names for the same wires on the sheet: M0 = Mask[0]; M1 = Mask[1]; M2 = Mask[2]; M3 = Mask[3];
  //   RW = nRead_Write; CLR = Reset; CS = Chip_Select; Load2 = Count

  // Notes on the sheet:
  //   NO MODIFICAR
  //   excepto quizás los valores RT y WT
  //   BANK0
  //   BANK1
  //   BANK2
  //   BANK3
endmodule

module S_MIPS (
  input  [15:0] Address,
  input  Kbd_Available,
  input  [6:0] Kbd_ASCII_Data,
  input  Reset,
  input  [31:0] RAM_In_0,
  input  [31:0] RAM_In_1,
  input  [31:0] RAM_In_2,
  input  [31:0] RAM_In_3,
  input  [3:0] Read_Time,
  input  [3:0] Write_Time,
  output Kbd_Enable,
  output Kbd_Clear,
  output [31:0] RAM_Out_0,
  output TTY_Enable,
  output [31:0] RAM_Out_1,
  output [6:0] TTY_ASCII_Data,
  output [31:0] RAM_Out_2,
  output Stop,
  output [31:0] RAM_Out_3,
  output [3:0] Mask,
  output nRead_Write,
  output Chip_Select
);

  wire Activation_Time_1, Activation_Time_2, Clock_1, Clock_2, instruction_decoder_1_clock_2,
       instruction_decoder_1_r___w, instruction_decoder_1_reset, Jmp;
  wire [3:0] counter_1_q, counter_2_q;
  wire [4:0] instruction_decoder_1_data_address, instruction_decoder_1_sa_2, instruction_decoder_1_sb_2;
  wire [15:0] instruction_decoder_1_constant;
  wire [31:0] ADDR, Inst, instruction_decoder_1_op_2, instruction_decoder_1_pc_2, PC, Pc_prime,
       Pc_prime_prime, Result;

  assign ADDR = {{16{1'b0}}, Address};  // Bit_Extender bit_extender_1
  Demultiplexer #(.select(2), .width(32)) demultiplexer_1 (
    .out0(RAM_Out_0), .out1(RAM_Out_1), .out2(RAM_Out_2), .out3(RAM_Out_3), .in(Result), .sel(PC[3:2]));  // open: en
  Multiplexer #(.select(2), .width(32)) multiplexer_1 (
    .in0(RAM_In_0), .in1(RAM_In_1), .in2(RAM_In_2), .in3(RAM_In_3), .out(Inst), .sel(PC[3:2]));  // open: en
  Counter #(.width(4), .max('hf)) counter_1 (.Q(counter_1_q), .clk(Clock_1));  // open: load, D, count, carry, clr
  Counter #(.width(4), .max('hf)) counter_2 (.Q(counter_2_q), .clk(Clock_2));  // open: load, D, count, carry, clr
  PC_3_0 pc_3_0_1 (
    .Clock_1(Activation_Time_1), .Clock_2(Activation_Time_2), .Rst(Reset), .ADDR(ADDR),
    .PC_prime_input(Pc_prime), .PC(PC), .PC_prime(Pc_prime_prime), .Jmp(Jmp));
  Clock u_clock_1 (.out(Clock_1));
  Clock u_clock_2 (.out(Clock_2));
  // Probe on counter_1_q
  Comparator #(.width(4)) comparator_1 (.a(counter_1_q), .b(Read_Time), .eq(Activation_Time_1));  // open: gt, lt
  // Probe on counter_2_q
  Comparator #(.width(4)) comparator_2 (.a(counter_2_q), .b(Write_Time), .eq(Activation_Time_2));  // open: gt, lt
  // Probe on PC
  // Probe on PC[3:2]
  Instruction_Decoder instruction_decoder_1 (
    .W_Id(nRead_Write), .Rst(Reset), .Instruction(Inst), .Clock(Clock_2), .Jmp(Jmp), .PC(PC),
    .Clock_2(instruction_decoder_1_clock_2), .R___W(instruction_decoder_1_r___w),
    .Data_Address(instruction_decoder_1_data_address), .Reset(instruction_decoder_1_reset),
    .Sa_2(instruction_decoder_1_sa_2), .Sb_2(instruction_decoder_1_sb_2),
    .Constant(instruction_decoder_1_constant), .Op_2(instruction_decoder_1_op_2),
    .PC_2(instruction_decoder_1_pc_2));  // open: Op, S_Mult, S_Div, SA, SB, DA, Mult, Div
  Data_Path data_path_1 (
    .Clock(instruction_decoder_1_clock_2), .RW(instruction_decoder_1_r___w),
    .DA(instruction_decoder_1_data_address), .Rst(instruction_decoder_1_reset),
    .SA(instruction_decoder_1_sa_2), .SB(instruction_decoder_1_sb_2), .Op(instruction_decoder_1_op_2),
    .Constant(instruction_decoder_1_constant), .Data_Output(Result), .Pc(instruction_decoder_1_pc_2),
    .Pc_prime(Pc_prime));  // open: A, B

  // Other names for the same wires on the sheet: CS = Chip_Select; KBD_AVAIL = Kbd_Available; KBD_CLR = Kbd_Clear;
  //   KBD_DATA[6:0] = Kbd_ASCII_Data; PC_value[1:0] = PC[3:2]; R1I[31:0] = RAM_In_0; R1O[31:0] = RAM_Out_0;
  //   R2I[31:0] = RAM_In_1; R2O[31:0] = RAM_Out_1; R3I[31:0] = RAM_In_2; R3O[31:0] = RAM_Out_2; R4I[31:0] = RAM_In_3;
  //   R4O[31:0] = RAM_Out_3; RAM_MASK[3:0] = Mask; Rst = Reset; TTY_DATA[6:0] = TTY_ASCII_Data; W_Id = nRead_Write

  // Notes on the sheet:
  //   RAM ADDRESS
  //   DATA FROM RAM
  //   DATA TO RAM
  //   DATA WRITE MASK
  //   RAM TIMING
  //   RAM CONTROL
  //   CU
  //   PC
  //   Timer Reader
  //   ID
  //   KEYBOARD
  //   TTY
  //   SEQUENCING
  //   Data Path
endmodule

module RAM_Dispatcher (
  input  [3:0] WriteTime,
  input  Clock,
  input  CLR,
  output [31:0] Data,
  output [15:0] Address,
  output [3:0] Mask,
  output Finished,
  output Write
);

  wire demultiplexer_2_out1, demultiplexer_3_out1, End, IDLE_q, IncAddr, Load, or_1_out, or_2_out, While_q,
       WriteEnd;
  wire [3:0] counter_1_q;
  wire [31:0] CurrentAddress_q;

  Counter #(.width(32), .max('hffffffff)) CurrentAddress (
    .count(IncAddr), .Q({CurrentAddress_q[31:18], Address, CurrentAddress_q[1:0]}), .clk(Clock), .clr(CLR));  // open: load, D, carry
  or or_1 (or_1_out, IncAddr, demultiplexer_3_out1, Finished);
  D_Flip_Flop IDLE (.clk(Clock), .D(or_1_out), .Q(IDLE_q), .preset(CLR));  // open: Qn, en, reset
  Demultiplexer #(.enable("false")) demultiplexer_1 (.out0(Load), .out1(Finished), .in(IDLE_q), .sel(End));
  D_Flip_Flop While (.clk(Clock), .D(or_2_out), .Q(While_q), .reset(CLR));  // open: Qn, preset, en
  or or_2 (or_2_out, Write, Load);
  RAM_part #(.addrWidth(18), .dataWidth(32)) ram_1 (
    .addr({Address, CurrentAddress_q[1:0]}), .data(Data), .clk(Clock));  // open: sel, ld, clr
  Demultiplexer #(.enable("false")) demultiplexer_2 (
    .out0(Write), .out1(demultiplexer_2_out1), .in(While_q), .sel(WriteEnd));
  Decoder #(.select(2)) decoder_1 (
    .out0(Mask[0]), .out1(Mask[1]), .out2(Mask[2]), .out3(Mask[3]), .sel(CurrentAddress_q[1:0]));  // open: en
  Demultiplexer #(.enable("false")) demultiplexer_3 (
    .out0(IncAddr), .out1(demultiplexer_3_out1), .in(demultiplexer_2_out1), .sel(End));
  Counter #(.width(4), .max('hf)) counter_1 (
    .load(Load), .D(WriteTime), .count(Write), .Q(counter_1_q), .clk(Clock));  // open: carry, clr
  Comparator #(.width(32)) comparator_1 (.a(Data), .b({32{1'b1}}), .eq(End));  // open: gt, lt
  Comparator #(.width(4)) comparator_2 (.a(4'b0000), .b(counter_1_q), .eq(WriteEnd));  // open: gt, lt

  // Other names for the same wires on the sheet: CLK = Clock; Count = Write; WT[3:0] = WriteTime
endmodule

module Central_Processing_Unit (
  input  [15:0] Address,
  input  Kbd_Available,
  input  [6:0] Kbd_ASCII_Data,
  input  Reset,
  input  [31:0] RAM_In_0,
  input  [31:0] RAM_In_1,
  input  [31:0] RAM_In_2,
  input  [31:0] RAM_In_3,
  input  [3:0] Read_Time,
  input  [3:0] Write_Time,
  output Kbd_Enable,
  output Kbd_Clear,
  output [31:0] RAM_Out_0,
  output TTY_Enable,
  output [31:0] RAM_Out_1,
  output [6:0] TTY_ASCII_Data,
  output [31:0] RAM_Out_2,
  output Stop,
  output [31:0] RAM_Out_3,
  output [3:0] Mask,
  output nRead_Write,
  output Chip_Select
);

  wire Activation_Time_1, Activation_Time_2, Clock_1, Clock_2, instruction_decoder_1_clock_2,
       instruction_decoder_1_r___w, instruction_decoder_1_reset, Jmp;
  wire [3:0] counter_1_q, counter_2_q;
  wire [4:0] instruction_decoder_1_data_address, instruction_decoder_1_sa_2, instruction_decoder_1_sb_2;
  wire [15:0] instruction_decoder_1_constant;
  wire [31:0] ADDR, Inst, instruction_decoder_1_op_2, instruction_decoder_1_pc_2, PC, Pc_prime,
       Pc_prime_prime, Result;

  assign ADDR = {{16{1'b0}}, Address};  // Bit_Extender bit_extender_1
  Demultiplexer #(.select(2), .width(32)) demultiplexer_1 (
    .out0(RAM_Out_0), .out1(RAM_Out_1), .out2(RAM_Out_2), .out3(RAM_Out_3), .in(Result), .sel(PC[3:2]));  // open: en
  Multiplexer #(.select(2), .width(32)) multiplexer_1 (
    .in0(RAM_In_0), .in1(RAM_In_1), .in2(RAM_In_2), .in3(RAM_In_3), .out(Inst), .sel(PC[3:2]));  // open: en
  Counter #(.width(4), .max('hf)) counter_1 (.Q(counter_1_q), .clk(Clock_1));  // open: load, D, count, carry, clr
  Counter #(.width(4), .max('hf)) counter_2 (.Q(counter_2_q), .clk(Clock_2));  // open: load, D, count, carry, clr
  PC_3_0 pc_3_0_1 (
    .Clock_1(Activation_Time_1), .Clock_2(Activation_Time_2), .Rst(Reset), .ADDR(ADDR),
    .PC_prime_input(Pc_prime), .PC(PC), .PC_prime(Pc_prime_prime), .Jmp(Jmp));
  Clock u_clock_1 (.out(Clock_1));
  Clock u_clock_2 (.out(Clock_2));
  // Probe on counter_1_q
  Comparator #(.width(4)) comparator_1 (.a(counter_1_q), .b(Read_Time), .eq(Activation_Time_1));  // open: gt, lt
  // Probe on counter_2_q
  Comparator #(.width(4)) comparator_2 (.a(counter_2_q), .b(Write_Time), .eq(Activation_Time_2));  // open: gt, lt
  // Probe on PC
  // Probe on PC[3:2]
  Instruction_Decoder instruction_decoder_1 (
    .W_Id(nRead_Write), .Rst(Reset), .Instruction(Inst), .Clock(Clock_2), .Jmp(Jmp), .PC(PC),
    .Clock_2(instruction_decoder_1_clock_2), .R___W(instruction_decoder_1_r___w),
    .Data_Address(instruction_decoder_1_data_address), .Reset(instruction_decoder_1_reset),
    .Sa_2(instruction_decoder_1_sa_2), .Sb_2(instruction_decoder_1_sb_2),
    .Constant(instruction_decoder_1_constant), .Op_2(instruction_decoder_1_op_2),
    .PC_2(instruction_decoder_1_pc_2));  // open: Op, S_Mult, S_Div, SA, SB, DA, Mult, Div
  Data_Path data_path_1 (
    .Clock(instruction_decoder_1_clock_2), .RW(instruction_decoder_1_r___w),
    .DA(instruction_decoder_1_data_address), .Rst(instruction_decoder_1_reset),
    .SA(instruction_decoder_1_sa_2), .SB(instruction_decoder_1_sb_2), .Op(instruction_decoder_1_op_2),
    .Constant(instruction_decoder_1_constant), .Data_Output(Result), .Pc(instruction_decoder_1_pc_2),
    .Pc_prime(Pc_prime));  // open: A, B

  // Other names for the same wires on the sheet: CS = Chip_Select; KBD_AVAIL = Kbd_Available; KBD_CLR = Kbd_Clear;
  //   KBD_DATA[6:0] = Kbd_ASCII_Data; PC_value[1:0] = PC[3:2]; R1I[31:0] = RAM_In_0; R1O[31:0] = RAM_Out_0;
  //   R2I[31:0] = RAM_In_1; R2O[31:0] = RAM_Out_1; R3I[31:0] = RAM_In_2; R3O[31:0] = RAM_Out_2; R4I[31:0] = RAM_In_3;
  //   R4O[31:0] = RAM_Out_3; RAM_MASK[3:0] = Mask; Rst = Reset; TTY_DATA[6:0] = TTY_ASCII_Data; W_Id = nRead_Write

  // Notes on the sheet:
  //   RAM ADDRESS
  //   DATA FROM RAM
  //   DATA TO RAM
  //   DATA WRITE MASK
  //   RAM TIMING
  //   RAM CONTROL
  //   CU
  //   PC
  //   Timer Reader
  //   ID
  //   KEYBOARD
  //   TTY
  //   SEQUENCING
  //   Data Path
endmodule

// Mux
module MacroMUX (
  input  [31:0] Data_Input_8,
  input  [31:0] Data_Input_0,
  input  [31:0] Data_Input_9,
  input  [31:0] Data_Input_1,
  input  [31:0] Data_Input_10,
  input  [31:0] Data_Input_2,
  input  [31:0] Data_Input_11,
  input  [31:0] Data_Input_3,
  input  [31:0] Data_Input_12,
  input  [31:0] Data_Input_4,
  input  [31:0] Data_Input_13,
  input  [31:0] Data_Input_5,
  input  [31:0] Data_Input_14,
  input  [31:0] Data_Input_6,
  input  [31:0] Data_Input_15,
  input  [31:0] Data_Input_7,
  input  [31:0] Data_Input_16,
  input  [31:0] Data_Input_24,
  input  [31:0] Data_Input_17,
  input  [31:0] Data_Input_25,
  input  [31:0] Selector,
  input  [31:0] Data_Input_18,
  input  [31:0] Data_Input_26,
  input  [31:0] Data_Input_19,
  input  [31:0] Data_Input_27,
  input  [31:0] Data_Input_20,
  input  [31:0] Data_Input_28,
  input  [31:0] Data_Input_21,
  input  [31:0] Data_Input_29,
  input  [31:0] Data_Input_22,
  input  [31:0] Data_Input_30,
  input  [31:0] Data_Input_23,
  input  [31:0] Data_Input_31,
  output [31:0] Output
);

  wire undriven;
  wire [4:0] priority_encoder_1_out;

  Multiplexer #(.select(5), .width(32)) multiplexer_1 (
    .in0(Data_Input_0), .in1(Data_Input_1), .in2(Data_Input_2), .in3(Data_Input_3), .in4(Data_Input_4),
    .in5(Data_Input_5), .in6(Data_Input_6), .in7(Data_Input_7), .in8(Data_Input_8), .in9(Data_Input_9),
    .in10(Data_Input_10), .in11(Data_Input_11), .in12(Data_Input_12), .in13(Data_Input_13),
    .in14(Data_Input_14), .in15(Data_Input_15), .in16(Data_Input_16), .in17(Data_Input_17),
    .in18(Data_Input_18), .in19(Data_Input_19), .in20(Data_Input_20), .in21(Data_Input_21),
    .in22(Data_Input_22), .in23(Data_Input_23), .in24(Data_Input_24), .in25(Data_Input_25),
    .in26(Data_Input_26), .in27(Data_Input_27), .in28(Data_Input_28), .in29(Data_Input_29),
    .in30(Data_Input_30), .in31(Data_Input_31), .out(Output), .sel(priority_encoder_1_out), .en(undriven));
  Priority_Encoder #(.select(5), .disabled(0)) priority_encoder_1 (
    .in0(Selector[0]), .in1(Selector[1]), .in2(Selector[2]), .in3(Selector[3]), .in4(Selector[4]),
    .in5(Selector[5]), .in6(Selector[6]), .in7(Selector[7]), .in8(Selector[8]), .in9(Selector[9]),
    .in10(Selector[10]), .in11(Selector[11]), .in12(Selector[12]), .in13(Selector[13]), .in14(Selector[14]),
    .in15(Selector[15]), .in16(Selector[16]), .in17(Selector[17]), .in18(Selector[18]), .in19(Selector[19]),
    .in20(Selector[20]), .in21(Selector[21]), .in22(Selector[22]), .in23(Selector[23]), .in24(Selector[24]),
    .in25(Selector[25]), .in26(Selector[26]), .in27(Selector[27]), .in28(Selector[28]), .in29(Selector[29]),
    .in30(Selector[30]), .in31(Selector[31]), .out(priority_encoder_1_out));
endmodule

module Register_File_x2 (
  input  Clock,
  input  [31:0] Data_Input,
  input  [4:0] SA,
  input  RW,
  input  Rst,
  input  [4:0] DA,
  input  [4:0] SB,
  input  [31:0] HI_Input,
  input  [31:0] LO_Input,
  input  HI___LO_enable,
  output [31:0] A,
  output [31:0] B,
  output [31:0] Hi_value,
  output [31:0] Lo_Value
);

  wire decoder_1_out1, decoder_1_out2, decoder_1_out3, decoder_1_out4, decoder_1_out5, decoder_1_out6,
       decoder_1_out7, decoder_1_out8, decoder_1_out9, decoder_1_out10, decoder_1_out11, decoder_1_out12,
       decoder_1_out13, decoder_1_out14, decoder_1_out15, not_1_out, not_2_out;
  wire [15:0] decoder_1_out16;
  wire [31:0] register_1_q, register_2_q, register_3_q, register_4_q, register_5_q, register_6_q,
       register_7_q, register_8_q, register_9_q, register_10_q, register_11_q, register_12_q, register_13_q,
       register_14_q, register_15_q, register_16_q, register_17_q, register_18_q, register_19_q,
       register_20_q, register_21_q, register_22_q, register_23_q, register_24_q, register_25_q,
       register_26_q, register_27_q, register_28_q, register_29_q, register_30_q, register_31_q,
       register_32_q;

  not not_1 (not_1_out, 1'b1);
  Decoder #(.select(5)) decoder_1 (
    .out1(decoder_1_out1), .out2(decoder_1_out2), .out3(decoder_1_out3), .out4(decoder_1_out4),
    .out5(decoder_1_out5), .out6(decoder_1_out6), .out7(decoder_1_out7), .out8(decoder_1_out8),
    .out9(decoder_1_out9), .out10(decoder_1_out10), .out11(decoder_1_out11), .out12(decoder_1_out12),
    .out13(decoder_1_out13), .out14(decoder_1_out14), .out15(decoder_1_out15), .out16(decoder_1_out16[0]),
    .out17(decoder_1_out16[1]), .out18(decoder_1_out16[2]), .out19(decoder_1_out16[3]),
    .out20(decoder_1_out16[4]), .out21(decoder_1_out16[5]), .out22(decoder_1_out16[6]),
    .out23(decoder_1_out16[7]), .out24(decoder_1_out16[8]), .out25(decoder_1_out16[9]),
    .out26(decoder_1_out16[10]), .out27(decoder_1_out16[11]), .out28(decoder_1_out16[12]),
    .out29(decoder_1_out16[13]), .out30(decoder_1_out16[14]), .out31(decoder_1_out16[15]), .sel(DA), .en(RW));  // open: out0
  Register #(.width(32)) register_1 (.D(Data_Input), .en(not_1_out), .Q(register_1_q), .clk(Clock), .clr(not_2_out));
  Register #(.width(32)) register_2 (.D(Data_Input), .en(decoder_1_out1), .Q(register_2_q), .clk(Clock), .clr(Rst));
  Register #(.width(32)) register_3 (.D(Data_Input), .en(decoder_1_out2), .Q(register_3_q), .clk(Clock), .clr(Rst));
  Register #(.width(32)) register_4 (.D(Data_Input), .en(decoder_1_out3), .Q(register_4_q), .clk(Clock), .clr(Rst));
  Register #(.width(32)) register_5 (.D(Data_Input), .en(decoder_1_out4), .Q(register_5_q), .clk(Clock), .clr(Rst));
  Register #(.width(32)) register_6 (.D(Data_Input), .en(decoder_1_out6), .Q(register_6_q), .clk(Clock), .clr(Rst));
  Register #(.width(32)) register_7 (.D(Data_Input), .en(decoder_1_out7), .Q(register_7_q), .clk(Clock), .clr(Rst));
  Register #(.width(32)) register_8 (.D(Data_Input), .en(decoder_1_out8), .Q(register_8_q), .clk(Clock), .clr(Rst));
  Register #(.width(32)) register_9 (.D(Data_Input), .en(decoder_1_out5), .Q(register_9_q), .clk(Clock), .clr(Rst));
  Register #(.width(32)) register_10 (.D(Data_Input), .en(decoder_1_out9), .Q(register_10_q), .clk(Clock), .clr(Rst));
  Register #(.width(32)) register_11 (.D(Data_Input), .en(decoder_1_out10), .Q(register_11_q), .clk(Clock), .clr(Rst));
  Register #(.width(32)) register_12 (.D(Data_Input), .en(decoder_1_out11), .Q(register_12_q), .clk(Clock), .clr(Rst));
  Register #(.width(32)) register_13 (.D(Data_Input), .en(decoder_1_out12), .Q(register_13_q), .clk(Clock), .clr(Rst));
  Register #(.width(32)) register_14 (.D(Data_Input), .en(decoder_1_out13), .Q(register_14_q), .clk(Clock), .clr(Rst));
  Register #(.width(32)) register_15 (.D(Data_Input), .en(decoder_1_out14), .Q(register_15_q), .clk(Clock), .clr(Rst));
  Register #(.width(32)) register_16 (.D(Data_Input), .en(decoder_1_out15), .Q(register_16_q), .clk(Clock), .clr(Rst));
  Hi hi_1 (.Input(HI_Input), .Enable(HI___LO_enable), .Output(Hi_value), .Clock(Clock));
  Lo lo_1 (.Input(LO_Input), .Enable(HI___LO_enable), .Clock(Clock), .Output(Lo_Value));
  not not_2 (not_2_out, 1'b1);
  Register #(.width(32)) register_17 (
    .D(Data_Input), .en(decoder_1_out16[0]), .Q(register_17_q), .clk(Clock), .clr(Rst));
  Register #(.width(32)) register_18 (
    .D(Data_Input), .en(decoder_1_out16[1]), .Q(register_18_q), .clk(Clock), .clr(Rst));
  Register #(.width(32)) register_19 (
    .D(Data_Input), .en(decoder_1_out16[2]), .Q(register_19_q), .clk(Clock), .clr(Rst));
  Register #(.width(32)) register_20 (
    .D(Data_Input), .en(decoder_1_out16[3]), .Q(register_20_q), .clk(Clock), .clr(Rst));
  Register #(.width(32)) register_21 (
    .D(Data_Input), .en(decoder_1_out16[4]), .Q(register_21_q), .clk(Clock), .clr(Rst));
  Register #(.width(32)) register_22 (
    .D(Data_Input), .en(decoder_1_out16[5]), .Q(register_22_q), .clk(Clock), .clr(Rst));
  Register #(.width(32)) register_23 (
    .D(Data_Input), .en(decoder_1_out16[6]), .Q(register_23_q), .clk(Clock), .clr(Rst));
  Register #(.width(32)) register_24 (
    .D(Data_Input), .en(decoder_1_out16[7]), .Q(register_24_q), .clk(Clock), .clr(Rst));
  Register #(.width(32)) register_25 (
    .D(Data_Input), .en(decoder_1_out16[8]), .Q(register_25_q), .clk(Clock), .clr(Rst));
  Register #(.width(32)) register_26 (
    .D(Data_Input), .en(decoder_1_out16[9]), .Q(register_26_q), .clk(Clock), .clr(Rst));
  Register #(.width(32)) register_27 (
    .D(Data_Input), .en(decoder_1_out16[10]), .Q(register_27_q), .clk(Clock), .clr(Rst));
  Register #(.width(32)) register_28 (
    .D(Data_Input), .en(decoder_1_out16[11]), .Q(register_28_q), .clk(Clock), .clr(Rst));
  Register #(.width(32)) register_29 (
    .D(Data_Input), .en(decoder_1_out16[12]), .Q(register_29_q), .clk(Clock), .clr(Rst));
  Register #(.width(32)) register_30 (
    .D(Data_Input), .en(decoder_1_out16[13]), .Q(register_30_q), .clk(Clock), .clr(Rst));
  Register #(.width(32)) register_31 (
    .D(Data_Input), .en(decoder_1_out16[14]), .Q(register_31_q), .clk(Clock), .clr(Rst));
  Register #(.width(32)) register_32 (
    .D(Data_Input), .en(decoder_1_out16[15]), .Q(register_32_q), .clk(Clock), .clr(Rst));
  Multiplexer #(.select(5), .width(32)) multiplexer_1 (
    .in0(register_1_q), .in1(register_2_q), .in2(register_3_q), .in3(register_4_q), .in4(register_5_q),
    .in5(register_6_q), .in6(register_7_q), .in7(register_8_q), .in8(register_9_q), .in9(register_10_q),
    .in10(register_11_q), .in11(register_12_q), .in12(register_13_q), .in13(register_14_q),
    .in14(register_15_q), .in15(register_16_q), .in16(register_17_q), .in17(register_18_q),
    .in18(register_19_q), .in19(register_20_q), .in20(register_21_q), .in21(register_22_q),
    .in22(register_23_q), .in23(register_24_q), .in24(register_25_q), .in25(register_26_q),
    .in26(register_27_q), .in27(register_28_q), .in28(register_29_q), .in29(register_30_q),
    .in30(register_31_q), .in31(register_32_q), .out(A), .sel(SA));  // open: en
  Multiplexer #(.select(5), .width(32)) multiplexer_2 (
    .in0(register_1_q), .in1(register_2_q), .in2(register_3_q), .in3(register_4_q), .in4(register_5_q),
    .in5(register_6_q), .in6(register_7_q), .in7(register_8_q), .in8(register_9_q), .in9(register_10_q),
    .in10(register_11_q), .in11(register_12_q), .in12(register_13_q), .in13(register_14_q),
    .in14(register_15_q), .in15(register_16_q), .in16(register_17_q), .in17(register_18_q),
    .in18(register_19_q), .in19(register_20_q), .in20(register_21_q), .in21(register_22_q),
    .in22(register_23_q), .in23(register_24_q), .in24(register_25_q), .in25(register_26_q),
    .in26(register_27_q), .in27(register_28_q), .in28(register_29_q), .in29(register_30_q),
    .in30(register_31_q), .in31(register_32_q), .out(B), .sel(SB));  // open: en
endmodule

// ALU
module ALU_2_0 (
  input  [31:0] A,
  input  [31:0] B,
  input  [15:0] Constant,
  input  [31:0] Op,
  output [31:0] Output,
  output [31:0] Hi_Value,
  output [31:0] Lo_Value,
  output Hi___LO_was_used
);

  wire and_2_out, and_3_out, and_4_out, and_5_out;
  wire [0:0] c3;
  wire [1:0] MUX, not_3_out, not_4_out, not_5_out, not_6_out, O1, O2, O3, O4;
  wire [1:1] c2;
  wire [31:0] _0, _1, _2, _3, adder_1_out, adder_2_out, And_out, Andi_out, bit_extender_1_out, divider_1_out,
       multiplexer_5_out, multiplier_1_out, Nor_out, Or_out, Ori_out, slt_1_output, slti_1_output,
       sltiu_1_output, subtractor_1_out, unsigned_div_1_output, unsigned_mult_1_output,
       unsigned_slt_1_output, Xor_out, Xori_out;

  not not_1 (c2[1], 1'b1);
  not not_2 (c3[0], 1'b1);
  assign bit_extender_1_out = {{16{1'b0}}, Constant};  // Bit_Extender bit_extender_1
  Adder #(.width(32)) adder_1 (.a(A), .b(B), .out(adder_1_out));  // open: cin, cout
  Subtractor #(.width(32)) subtractor_1 (.a(A), .b(B), .out(subtractor_1_out));  // open: bin, bout
  Multiplier #(.width(32)) multiplier_1 (.a(A), .b(B), .out(multiplier_1_out), .cout(_0));  // open: cin
  Unsigned_Mult unsigned_mult_1 (.in_1(A), .in_2(B), .Output(unsigned_mult_1_output), .Output_2(_1));
  Divider #(.width(32)) divider_1 (.a(A), .b(B), .out(divider_1_out), .rem(_2));  // open: upper
  Unsigned_Div unsigned_div_1 (.in_1(A), .in_2(B), .Output(unsigned_div_1_output), .Output_2(_3));
  Adder #(.width(32)) adder_2 (.a(A), .b(bit_extender_1_out), .out(adder_2_out));  // open: cin, cout
  assign And_out = A & B;  // AND_Gate And, 32 bits wide
  assign Or_out = A | B;  // OR_Gate Or, 32 bits wide
  assign Nor_out = ~(A | B);  // NOR_Gate Nor, 32 bits wide
  assign Xor_out = A ^ B;  // XOR_Gate Xor, 32 bits wide
  assign Andi_out = A & bit_extender_1_out;  // AND_Gate Andi, 32 bits wide
  assign Ori_out = A | bit_extender_1_out;  // OR_Gate Ori, 32 bits wide
  assign Xori_out = A ^ bit_extender_1_out;  // XOR_Gate Xori, 32 bits wide
  Slt slt_1 (.Rs(A), .Rt(B), .Output(slt_1_output));
  Unsigned_Slt unsigned_slt_1 (.Rs(A), .Rt(B), .Output(unsigned_slt_1_output));
  Slti slti_1 (.Rs(A), .Constant(bit_extender_1_out), .Output(slti_1_output));
  Sltiu sltiu_1 (.Rs(A), .Constant(bit_extender_1_out), .Output(sltiu_1_output));
  assign not_3_out = ~2'b11;  // NOT_Gate not_3, 2 bits wide
  and and_2 (and_2_out, Op[2], ~Op[3], ~Op[4], ~Op[5]);  // AND_Gate
  assign not_4_out = ~2'b11;  // NOT_Gate not_4, 2 bits wide
  and and_3 (and_3_out, ~Op[2], Op[3], ~Op[4], ~Op[5]);  // AND_Gate
  assign not_5_out = ~2'b11;  // NOT_Gate not_5, 2 bits wide
  and and_4 (and_4_out, ~Op[2], ~Op[3], Op[4], ~Op[5]);  // AND_Gate
  assign not_6_out = ~2'b11;  // NOT_Gate not_6, 2 bits wide
  and and_5 (and_5_out, ~Op[2], ~Op[3], ~Op[4], Op[5]);  // AND_Gate
  Multiplexer #(.width(2)) multiplexer_1 (.in0(not_3_out), .in1(not_3_out), .out(O1), .sel(and_2_out));  // open: en
  Multiplexer #(.width(2)) multiplexer_2 (.in0(not_4_out), .in1({c2[1], 1'b1}), .out(O2), .sel(and_3_out));  // open: en
  Multiplexer #(.width(2)) multiplexer_3 (.in0(not_5_out), .in1({1'b1, c3[0]}), .out(O3), .sel(and_4_out));  // open: en
  Multiplexer #(.width(2)) multiplexer_4 (.in0(not_6_out), .in1(2'b11), .out(O4), .sel(and_5_out));  // open: en
  or or_2 (Hi___LO_was_used, Op[2], Op[3], Op[4], Op[5]);
  Multiplexer #(.select(2), .width(32)) multiplexer_5 (
    .in0(_0), .in1(_1), .in2(_2), .in3(_3), .out(multiplexer_5_out), .sel(MUX));  // open: en
  assign MUX = O1 | O2 | O3 | O4;  // OR_Gate or_3, 2 bits wide
  MacroMUX macromux_1 (
    .Data_Input_8(Or_out), .Data_Input_0(adder_1_out), .Data_Input_9(Nor_out),
    .Data_Input_1(subtractor_1_out), .Data_Input_10(Xor_out), .Data_Input_2(multiplier_1_out),
    .Data_Input_11(Andi_out), .Data_Input_3(unsigned_mult_1_output), .Data_Input_12(Ori_out),
    .Data_Input_4(divider_1_out), .Data_Input_13(Xori_out), .Data_Input_5(unsigned_div_1_output),
    .Data_Input_14(slt_1_output), .Data_Input_6(adder_2_out), .Data_Input_15(unsigned_slt_1_output),
    .Data_Input_7(And_out), .Data_Input_16(slti_1_output), .Data_Input_17(sltiu_1_output),
    .Data_Input_20(bit_extender_1_out), .Output(Output), .Selector(Op));  // open: Data_Input_24, Data_Input_25, Data_Input_18, Data_Input_26, Data_Input_19, Data_Input_27, Data_Input_28, Data_Input_21, Data_Input_29, Data_Input_22, Data_Input_30, Data_Input_23, Data_Input_31
  // Probe on MUX
  Hi hi_1 (.Input(Output), .Enable(Hi___LO_was_used), .Output(Hi_Value), .Clock(Hi___LO_was_used));
  Lo lo_1 (.Input(multiplexer_5_out), .Enable(Hi___LO_was_used), .Clock(Hi___LO_was_used), .Output(Lo_Value));

  // Other names for the same wires on the sheet: a_t = Op[2]; b_t = Op[3]; c = Op[4]; d = Op[5]

  // Notes on the sheet:
  //   nop
  //   Operaciones Aritmético-Logicas
  //   Lógica de guardado para registros Hi y LO
endmodule

module Data_Path (
  input  Clock,
  input  RW,
  input  [4:0] DA,
  input  Rst,
  input  [4:0] SA,
  input  [4:0] SB,
  input  [31:0] Op,
  input  [15:0] Constant,
  input  [31:0] Pc,
  output [31:0] Data_Output,
  output [31:0] A,
  output [31:0] B,
  output [31:0] Pc_prime
);

  wire alu_2_0_1_hi___lo_was_used;
  wire [31:0] alu_2_0_1_hi_value, alu_2_0_1_lo_value;

  Register_File_x2 register_file_x2_1 (
    .Data_Input(Data_Output), .A(A), .B(B), .RW(RW), .DA(DA), .Rst(Rst), .SA(SA), .SB(SB), .Clock(Clock),
    .HI_Input(alu_2_0_1_hi_value), .LO_Input(alu_2_0_1_lo_value), .HI___LO_enable(alu_2_0_1_hi___lo_was_used));  // open: Hi_value, Lo_Value
  ALU_2_0 alu_2_0_1 (
    .A(A), .B(B), .Constant(Constant), .Op(Op), .Output(Data_Output), .Hi_Value(alu_2_0_1_hi_value),
    .Lo_Value(alu_2_0_1_lo_value), .Hi___LO_was_used(alu_2_0_1_hi___lo_was_used));
  Bc_1_0 bc_1_0_1 (.Js(Constant), .Pc(Pc), .PC_prime(Pc_prime), .Op(Op), .A(A), .B(B));
endmodule

// ID
module Instruction_Decoder (
  input  [31:0] Instruction,
  input  W_Id,
  input  Clock,
  input  Rst,
  input  [31:0] PC,
  output [31:0] Op,
  output S_Mult,
  output S_Div,
  output Mult,
  output Div,
  output [4:0] SA,
  output [4:0] SB,
  output [4:0] DA,
  output Clock_2,
  output R___W,
  output [4:0] Data_Address,
  output Reset,
  output [4:0] Sa_2,
  output [31:0] Op_2,
  output [4:0] Sb_2,
  output [15:0] Constant,
  output Jmp,
  output [31:0] PC_2
);

  wire or_3_out;
  wire [4:0] not_2_out;
  wire [15:0] not_3_out;

  Sum_Bool sum_bool_1 (.in_1({Instruction[10:0], Instruction[31:26]}), .Output(Op[0]));
  Rest_Bool rest_bool_1 (.in_1({Instruction[10:0], Instruction[31:26]}), .Output(Op[1]));
  Mult_Bool mult_bool_1 (.in_1({Instruction[31:26], Instruction[15:0]}), .Output(Op[2]));
  MULU_bool mulu_bool_1 (.in_1({Instruction[31:26], Instruction[15:0]}), .Output(Op[3]));
  DIV_bool div_bool_1 (.in_1({Instruction[31:26], Instruction[15:0]}), .Output(Op[4]));
  Unsigned_Div_Bool unsigned_div_bool_1 (.in_1({Instruction[31:26], Instruction[15:0]}), .Output(Op[5]));
  Addi_Bool addi_bool_1 (.in_1(Instruction[31:26]), .Output(Op[6]));
  And_Bool and_bool_1 (
    .in_1({Instruction[10:3], Instruction[31], Instruction[2:0], Instruction[30:26]}), .Output(Op[7]));
  Or_Bool or_bool_1 (.in_1({Instruction[10:3], Instruction[31], Instruction[2:0], Instruction[30:26]}), .Output(Op[8]));
  Nor_Bool nor_bool_1 (
    .in_1({Instruction[10:3], Instruction[31], Instruction[2:0], Instruction[30:26]}), .Output(Op[9]));
  Xor_Bool xor_bool_1 (
    .in_1({Instruction[10:3], Instruction[31], Instruction[2:0], Instruction[30:26]}), .Output(Op[10]));
  Andi_Bool andi_bool_1 (.in_1(Instruction[31:26]), .Output(Op[11]));
  Ori_Bool ori_bool_1 (.in_1(Instruction[31:26]), .Output(Op[12]));
  Xori_Bool xori_bool_1 (.in_1(Instruction[31:26]), .Output(Op[13]));
  Slt_Bool slt_bool_1 (.in_1({Instruction[31:26], Instruction[15:0]}), .Output(Op[14]));
  Unsigned_Slt_Bool unsigned_slt_bool_1 (.in_1({Instruction[31:26], Instruction[15:0]}), .Output(Op[15]));
  Slti_Bool slti_bool_1 (.in_1(Instruction[31:26]), .Output(Op[16]));
  Sltiu_Bool sltiu_bool_1 (.in_1(Instruction[31:26]), .Output(Op[17]));
  Mfhi_Bool mfhi_bool_1 (.in_1({Instruction[31:16], Instruction[10:0]}), .Output(Op[18]));
  Mflo_Bool mflo_bool_1 (.in_1({Instruction[31:16], Instruction[10:0]}), .Output(Op[19]));
  nop nop_1 (.in_1({Instruction[15:11], Instruction[31:16], Instruction[10:0]}), .Output(Op[20]));
  Beq_Bool beq_bool_1 (.in_1(Instruction[31:26]), .Output(Op[21]));
  Bne_Bool bne_bool_1 (.in_1(Instruction[31:26]), .Output(Op[22]));
  Blez_Bool blez_bool_1 (.in_1(Instruction[31:26]), .Output(Op[23]));
  Bgtz_Bool bgtz_bool_1 (.in_1(Instruction[31:26]), .Output(Op[24]));
  Bltz_Bool bltz_bool_1 (.in_1(Instruction[31:26]), .Output(Op[25]));
  Jump_Bool jump_bool_1 (.in_1(Instruction[31:26]), .Output(Op[26]));
  Jr_Bool jr_bool_1 ();  // open: in_1, Output
  or or_1 (Mult, Op[3], Op[2]);
  or or_2 (Div, Op[4], Op[5]);
  not not_1 (Op[31], 1'b1);
  or or_3 (or_3_out, Op[0], Op[1], Op[2], Op[3], Op[4], Op[5], Op[7], Op[8], Op[9], Op[10], Op[15], Op[14]);
  or or_4 (Jmp, Op[21], Op[22], Op[23], Op[24], Op[26], Op[31], Op[31], Op[25]);
  // Probe on Instruction[15:0]
  assign not_2_out = ~{5{1'b1}};  // NOT_Gate not_2, 5 bits wide
  assign not_3_out = ~{16{1'b1}};  // NOT_Gate not_3, 16 bits wide
  Multiplexer #(.width(5)) multiplexer_1 (
    .in0(Instruction[25:21]), .in1(Instruction[20:16]), .out(SA), .sel(or_3_out));  // open: en
  Multiplexer #(.width(5)) multiplexer_2 (
    .in0(not_2_out), .in1(Instruction[25:21]), .out(SB), .sel(or_3_out));  // open: en
  Multiplexer #(.width(5)) multiplexer_3 (
    .in0(Instruction[20:16]), .in1(Instruction[15:11]), .out(DA), .sel(or_3_out));  // open: en
  Multiplexer #(.width(16)) multiplexer_4 (
    .in0(Instruction[15:0]), .in1(not_3_out), .out(Constant), .sel(or_3_out));  // open: en
  // Probe on {{5{Op[31]}}, Op[26:0]}

  assign Clock_2 = Clock;
  assign Data_Address = DA;
  assign Op[30:27] = {4{Op[31]}};
  assign Op_2 = {{5{Op[31]}}, Op[26:0]};
  assign PC_2 = PC;
  assign R___W = W_Id;
  assign Reset = Rst;
  assign S_Div = Div;
  assign S_Mult = Mult;
  assign Sa_2 = SA;
  assign Sb_2 = SB;
endmodule

// Bc
module Bc_1_0 (
  input  [31:0] A,
  input  [31:0] B,
  input  [15:0] Js,
  input  [31:0] Op,
  input  [31:0] Pc,
  output [31:0] PC_prime
);

  wire [31:0] beq_1_pc_prime, undriven;

  Beq beq_1 (.A(A), .B(B), .PC(Pc), .Js(Js), .PC_prime(beq_1_pc_prime));
  MacroMUX macromux_1 (
    .Data_Input_27(undriven), .Data_Input_21(beq_1_pc_prime), .Output(PC_prime), .Selector(Op));  // open: Data_Input_8, Data_Input_0, Data_Input_9, Data_Input_1, Data_Input_10, Data_Input_2, Data_Input_11, Data_Input_3, Data_Input_12, Data_Input_4, Data_Input_13, Data_Input_5, Data_Input_14, Data_Input_6, Data_Input_15, Data_Input_7, Data_Input_16, Data_Input_24, Data_Input_17, Data_Input_25, Data_Input_18, Data_Input_26, Data_Input_19, Data_Input_20, Data_Input_28, Data_Input_29, Data_Input_22, Data_Input_30, Data_Input_23, Data_Input_31
endmodule

// C2
module PC_2_0 (
  input  [31:0] Input,
  output [31:0] Sum
);

  wire [2:2] not_2_out;
  wire [15:0] not_1_out;
  wire [31:0] bit_extender_1_out;

  assign not_1_out = ~{16{1'b1}};  // NOT_Gate not_1, 16 bits wide
  not not_2 (not_2_out[2], not_1_out[2]);
  assign bit_extender_1_out = {{16{1'b0}}, {not_1_out[15:3], not_2_out[2], not_1_out[1:0]}};  // Bit_Extender bit_extender_1
  Adder #(.width(32)) adder_1 (.a(Input), .b(bit_extender_1_out), .out(Sum));  // open: cin, cout

  // Notes on the sheet:
  //   Sumador del PC por defecto (sumar 4)
endmodule

// PC
module PC_3_0 (
  input  Clock_1,
  input  Clock_2,
  input  Rst,
  input  [31:0] ADDR,
  input  [31:0] PC_prime_input,
  input  Jmp,
  output [31:0] PC,
  output [31:0] PC_prime
);

  wire counter_1_q;
  wire [31:0] multiplexer_1_out, multiplexer_2_out, pc_2_0_1_sum;

  Counter #(.width(1), .max('h1), .ongoal("stay")) counter_1 (
    .Q(counter_1_q), .clk(Clock_1), .clr(Rst));  // open: load, D, count, carry
  Multiplexer #(.width(32)) multiplexer_1 (
    .in0(ADDR), .in1(PC_prime), .out(multiplexer_1_out), .sel(counter_1_q));  // open: en
  // Probe on PC
  Register #(.width(32)) Dir_1 (.D(multiplexer_1_out), .Q(PC), .clk(Clock_1), .clr(Rst));  // open: en
  PC_2_0 pc_2_0_1 (.Input(PC), .Sum(pc_2_0_1_sum));
  Multiplexer #(.width(32)) multiplexer_2 (
    .in0(pc_2_0_1_sum), .in1(PC_prime_input), .out(multiplexer_2_out), .sel(Jmp));  // open: en
  Register #(.width(32)) Dir_2 (.D(multiplexer_2_out), .Q(PC_prime), .clk(Clock_2), .clr(Rst));  // open: en

  // Notes on the sheet:
  //   Program Counter 
endmodule

// HI
module Hi (
  input  [31:0] Input,
  input  Enable,
  input  Clock,
  output [31:0] Output
);

  Register #(.width(32)) register_1 (.D(Input), .en(Enable), .Q(Output), .clk(Clock));  // open: clr
endmodule

// LO
module Lo (
  input  [31:0] Input,
  input  Enable,
  input  Clock,
  output [31:0] Output
);

  Register #(.width(32)) register_1 (.D(Input), .en(Enable), .Q(Output), .clk(Clock));  // open: clr
endmodule

// +
module Sum_Bool (
  input  [16:0] in_1,
  output Output
);

  wire not_1_out, not_2_out, not_3_out, not_4_out, not_5_out, not_6_out, not_7_out, not_8_out, not_9_out,
       not_10_out, not_11_out, not_12_out, not_13_out, not_14_out, not_15_out, not_16_out;

  not not_1 (not_1_out, in_1[0]);
  not not_2 (not_2_out, in_1[1]);
  not not_3 (not_3_out, in_1[2]);
  not not_4 (not_4_out, in_1[3]);
  not not_5 (not_5_out, in_1[4]);
  not not_6 (not_6_out, in_1[5]);
  not not_7 (not_7_out, in_1[6]);
  not not_8 (not_8_out, in_1[7]);
  and and_1 (Output, not_1_out, not_2_out, not_3_out, not_4_out, not_5_out, not_6_out, not_7_out, not_8_out, not_9_out, not_10_out, not_11_out, in_1[11], not_12_out, not_13_out, not_14_out, not_15_out, not_16_out);
  not not_9 (not_9_out, in_1[8]);
  not not_10 (not_10_out, in_1[9]);
  not not_11 (not_11_out, in_1[10]);
  not not_12 (not_12_out, in_1[12]);
  not not_13 (not_13_out, in_1[13]);
  not not_14 (not_14_out, in_1[14]);
  not not_15 (not_15_out, in_1[15]);
  not not_16 (not_16_out, in_1[16]);
endmodule

// -
module Rest_Bool (
  input  [16:0] in_1,
  output Output
);

  and and_1 (Output, ~in_1[0], ~in_1[1], ~in_1[2], ~in_1[3], ~in_1[4], ~in_1[5], ~in_1[6], in_1[7], ~in_1[8], ~in_1[9], ~in_1[10], in_1[11], ~in_1[12], ~in_1[13], ~in_1[14], ~in_1[15], ~in_1[16]);  // AND_Gate
endmodule

// *
module Mult_Bool (
  input  [21:0] in_1,
  output Output
);

  wire not_1_out, not_2_out, or_1_out, or_2_out;

  not not_1 (not_1_out, or_1_out);
  or or_1 (or_1_out, in_1[0], in_1[1], in_1[2], ~in_1[3], ~in_1[4], in_1[5]);  // OR_Gate
  not not_2 (not_2_out, or_2_out);
  or or_2 (or_2_out, in_1[6], in_1[7], in_1[8], in_1[9], in_1[10], in_1[11], in_1[12], in_1[13], in_1[14], in_1[15], in_1[16], in_1[17], in_1[18], in_1[19], in_1[20], in_1[21]);
  and and_1 (Output, not_1_out, not_2_out);
endmodule

// **
module MULU_bool (
  input  [21:0] in_1,
  output Output
);

  wire not_1_out, not_2_out, or_1_out, or_2_out;

  or or_1 (or_1_out, ~in_1[0], in_1[1], in_1[2], ~in_1[3], ~in_1[4], in_1[5]);  // OR_Gate
  not not_1 (not_1_out, or_1_out);
  not not_2 (not_2_out, or_2_out);
  or or_2 (or_2_out, in_1[6], in_1[7], in_1[8], in_1[9], in_1[10], in_1[11], in_1[12], in_1[13], in_1[14], in_1[15], in_1[16], in_1[17], in_1[18], in_1[19], in_1[20], in_1[21]);
  and and_1 (Output, not_1_out, not_2_out);
endmodule

// /
module DIV_bool (
  input  [21:0] in_1,
  output Output
);

  wire not_1_out, not_2_out, or_1_out, or_2_out;

  not not_1 (not_1_out, or_1_out);
  or or_1 (or_1_out, in_1[0], ~in_1[1], in_1[2], ~in_1[3], ~in_1[4], in_1[5]);  // OR_Gate
  not not_2 (not_2_out, or_2_out);
  or or_2 (or_2_out, in_1[6], in_1[7], in_1[8], in_1[9], in_1[10], in_1[11], in_1[12], in_1[13], in_1[14], in_1[15], in_1[16], in_1[17], in_1[18], in_1[19], in_1[20], in_1[21]);
  and and_1 (Output, not_1_out, not_2_out);
endmodule

// //
module Unsigned_Div_Bool (
  input  [21:0] in_1,
  output Output
);

  wire not_1_out, not_2_out, or_1_out, or_2_out;

  or or_1 (or_1_out, ~in_1[0], ~in_1[1], in_1[2], ~in_1[3], ~in_1[4], in_1[5]);  // OR_Gate
  not not_1 (not_1_out, or_1_out);
  or or_2 (or_2_out, in_1[6], in_1[7], in_1[8], in_1[9], in_1[10], in_1[11], in_1[12], in_1[13], in_1[14], in_1[15], in_1[16], in_1[17], in_1[18], in_1[19], in_1[20], in_1[21]);
  not not_2 (not_2_out, or_2_out);
  and and_1 (Output, not_1_out, not_2_out);
endmodule

// ++
module Addi_Bool (
  input  [5:0] in_1,
  output Output
);

  wire or_1_out;

  or or_1 (or_1_out, in_1[0], in_1[1], in_1[2], ~in_1[3], in_1[4], in_1[5]);  // OR_Gate
  not not_1 (Output, or_1_out);
endmodule

// And
module And_Bool (
  input  [16:0] in_1,
  output Output
);

  wire or_1_out;

  or or_1 (or_1_out, in_1[0], in_1[1], in_1[2], in_1[3], in_1[4], in_1[5], in_1[6], ~in_1[7], in_1[8], in_1[9], in_1[10], ~in_1[11], in_1[12], in_1[13], in_1[14], in_1[15], in_1[16]);  // OR_Gate
  not not_1 (Output, or_1_out);
endmodule

// Or
module Or_Bool (
  input  [16:0] in_1,
  output Output
);

  wire or_1_out;

  not not_1 (Output, or_1_out);
  or or_1 (or_1_out, in_1[0], in_1[1], in_1[2], in_1[3], in_1[4], ~in_1[5], in_1[6], ~in_1[7], in_1[8], in_1[9], in_1[10], ~in_1[11], in_1[12], in_1[13], in_1[14], in_1[15], in_1[16]);  // OR_Gate
endmodule

// Nor
module Nor_Bool (
  input  [16:0] in_1,
  output Output
);

  wire or_1_out;

  or or_1 (or_1_out, in_1[0], in_1[1], in_1[2], in_1[3], in_1[4], ~in_1[5], ~in_1[6], ~in_1[7], in_1[8], in_1[9], in_1[10], ~in_1[11], in_1[12], in_1[13], in_1[14], in_1[15], in_1[16]);  // OR_Gate
  not not_1 (Output, or_1_out);
endmodule

// Xor
module Xor_Bool (
  input  [16:0] in_1,
  output Output
);

  wire or_1_out;

  not not_1 (Output, or_1_out);
  or or_1 (or_1_out, in_1[0], in_1[1], in_1[2], in_1[3], in_1[4], in_1[5], in_1[6], in_1[7], in_1[8], ~in_1[9], in_1[10], ~in_1[11], in_1[12], in_1[13], in_1[14], in_1[15], in_1[16]);  // OR_Gate
endmodule

// Andi
module Andi_Bool (
  input  [5:0] in_1,
  output Output
);

  wire or_1_out;

  or or_1 (or_1_out, in_1[0], in_1[1], ~in_1[2], ~in_1[3], in_1[4], in_1[5]);  // OR_Gate
  not not_1 (Output, or_1_out);
endmodule

// Ori
module Ori_Bool (
  input  [5:0] in_1,
  output Output
);

  wire or_1_out;

  or or_1 (or_1_out, ~in_1[0], in_1[1], ~in_1[2], ~in_1[3], in_1[4], in_1[5]);  // OR_Gate
  not not_1 (Output, or_1_out);
endmodule

// Xori
module Xori_Bool (
  input  [5:0] in_1,
  output Output
);

  wire or_1_out;

  or or_1 (or_1_out, in_1[0], ~in_1[1], ~in_1[2], ~in_1[3], in_1[4], in_1[5]);  // OR_Gate
  not not_1 (Output, or_1_out);
endmodule

// Slt
module Slt_Bool (
  input  [21:0] in_1,
  output Output
);

  wire or_1_out;

  or or_1 (or_1_out, in_1[0], ~in_1[1], in_1[2], ~in_1[3], in_1[4], ~in_1[5], in_1[6], in_1[7], in_1[8], in_1[9], in_1[10], in_1[12], in_1[13], in_1[14], in_1[15], in_1[16], in_1[17], in_1[18], in_1[19], in_1[20], in_1[21], in_1[11]);  // OR_Gate
  not not_1 (Output, or_1_out);
endmodule

// U/Slt
module Unsigned_Slt_Bool (
  input  [21:0] in_1,
  output Output
);

  wire or_1_out;

  or or_1 (or_1_out, ~in_1[0], ~in_1[1], in_1[2], ~in_1[3], in_1[4], ~in_1[5], in_1[6], in_1[7], in_1[8], in_1[9], in_1[10], in_1[12], in_1[13], in_1[14], in_1[15], in_1[16], in_1[17], in_1[18], in_1[19], in_1[20], in_1[21], in_1[11]);  // OR_Gate
  not not_1 (Output, or_1_out);
endmodule

// Slti
module Slti_Bool (
  input  [5:0] in_1,
  output Output
);

  wire or_1_out;

  or or_1 (or_1_out, in_1[0], ~in_1[1], in_1[2], in_1[4], in_1[5], ~in_1[3]);  // OR_Gate
  not not_1 (Output, or_1_out);
endmodule

// Sltiu
module Sltiu_Bool (
  input  [5:0] in_1,
  output Output
);

  wire or_1_out;

  or or_1 (or_1_out, ~in_1[0], ~in_1[1], in_1[2], in_1[4], in_1[5], ~in_1[3]);  // OR_Gate
  not not_1 (Output, or_1_out);
endmodule

// Mfhi
module Mfhi_Bool (
  input  [26:0] in_1,
  output Output
);

  wire or_1_out;

  or or_1 (or_1_out, in_1[0], in_1[1], in_1[2], in_1[3], ~in_1[4], in_1[5], in_1[6], in_1[7], in_1[8], in_1[9], in_1[10], in_1[11], in_1[12], in_1[13], in_1[14], in_1[15], in_1[16], in_1[17], in_1[18], in_1[19], in_1[20], in_1[21], in_1[22], in_1[23], in_1[24], in_1[25], in_1[26]);  // OR_Gate
  not not_1 (Output, or_1_out);
endmodule

// Mflo
module Mflo_Bool (
  input  [26:0] in_1,
  output Output
);

  wire or_1_out;

  or or_1 (or_1_out, in_1[0], ~in_1[1], in_1[2], in_1[3], ~in_1[4], in_1[5], in_1[6], in_1[7], in_1[8], in_1[9], in_1[10], in_1[11], in_1[12], in_1[13], in_1[14], in_1[15], in_1[16], in_1[17], in_1[18], in_1[19], in_1[20], in_1[21], in_1[22], in_1[23], in_1[24], in_1[25], in_1[26]);  // OR_Gate
  not not_1 (Output, or_1_out);
endmodule

// Beq
module Beq_Bool (
  input  [5:0] in_1,
  output Output
);

  wire or_1_out;

  or or_1 (or_1_out, in_1[0], in_1[1], ~in_1[2], in_1[4], in_1[5], in_1[3]);  // OR_Gate
  not not_1 (Output, or_1_out);
endmodule

// Bne
module Bne_bool (
  input  [5:0] in_1,
  output Output
);

  wire or_1_out;

  or or_1 (or_1_out, ~in_1[0], in_1[1], ~in_1[2], in_1[4], in_1[5], in_1[3]);  // OR_Gate
  not not_1 (Output, or_1_out);
endmodule

// Bne
module Bne_Bool (
  input  [5:0] in_1,
  output Output
);

  wire or_1_out;

  or or_1 (or_1_out, ~in_1[0], in_1[1], ~in_1[2], in_1[4], in_1[5], in_1[3]);  // OR_Gate
  not not_1 (Output, or_1_out);
endmodule

// Blez
module Blez_Bool (
  input  [5:0] in_1,
  output Output
);

  wire or_1_out;

  or or_1 (or_1_out, in_1[0], ~in_1[1], ~in_1[2], in_1[4], in_1[5], in_1[3]);  // OR_Gate
  not not_1 (Output, or_1_out);
endmodule

// Bgtz
module Bgtz_Bool (
  input  [5:0] in_1,
  output Output
);

  wire or_1_out;

  or or_1 (or_1_out, ~in_1[0], ~in_1[1], ~in_1[2], in_1[4], in_1[5], in_1[3]);  // OR_Gate
  not not_1 (Output, or_1_out);
endmodule

// Bltz
module Bltz_Bool (
  input  [5:0] in_1,
  output Output
);

  wire or_1_out;

  or or_1 (or_1_out, ~in_1[0], in_1[1], in_1[2], in_1[4], in_1[5], in_1[3]);  // OR_Gate
  not not_1 (Output, or_1_out);
endmodule

// Jump
module Jump_Bool (
  input  [5:0] in_1,
  output Output
);

  wire or_1_out;

  or or_1 (or_1_out, in_1[0], ~in_1[1], in_1[2], in_1[4], in_1[5], in_1[3]);  // OR_Gate
  not not_1 (Output, or_1_out);
endmodule

// Jr
module Jr_Bool (
  input  [26:0] in_1,
  output Output
);

  wire or_1_out;

  or or_1 (or_1_out, in_1[0], in_1[1], in_1[2], ~in_1[3], in_1[4], in_1[5], in_1[6], in_1[7], in_1[8], in_1[9], in_1[10], in_1[11], in_1[12], in_1[13], in_1[14], in_1[15], in_1[16], in_1[17], in_1[18], in_1[19], in_1[20], in_1[21], in_1[22], in_1[23], in_1[24], in_1[25], in_1[26]);  // OR_Gate
  not not_1 (Output, or_1_out);
endmodule

// Mult
module Unsigned_Mult (
  input  [31:0] in_1,
  input  [31:0] in_2,
  output [31:0] Output,
  output [31:0] Output_2
);

  wire [31:0] complemento_a_2_1_output, complemento_a_2_2_output, multiplexer_1_out, multiplexer_2_out;

  Complemento_a_2 complemento_a_2_1 (.Input(in_1), .Output(complemento_a_2_1_output));
  Complemento_a_2 complemento_a_2_2 (.Input(in_2), .Output(complemento_a_2_2_output));
  Multiplexer #(.width(32)) multiplexer_1 (
    .in0(in_1), .in1(complemento_a_2_1_output), .out(multiplexer_1_out), .sel(in_1[31]));  // open: en
  Multiplexer #(.width(32)) multiplexer_2 (
    .in0(in_2), .in1(complemento_a_2_2_output), .out(multiplexer_2_out), .sel(in_2[31]));  // open: en
  Multiplier #(.width(32)) multiplier_1 (
    .a(multiplexer_1_out), .b(multiplexer_2_out), .out(Output), .cout(Output_2));  // open: cin
endmodule

// Div
module Unsigned_Div (
  input  [31:0] in_1,
  input  [31:0] in_2,
  output [31:0] Output,
  output [31:0] Output_2
);

  wire [31:0] complemento_a_2_1_output, complemento_a_2_2_output, multiplexer_1_out, multiplexer_2_out;

  Complemento_a_2 complemento_a_2_1 (.Input(in_1), .Output(complemento_a_2_1_output));
  Complemento_a_2 complemento_a_2_2 (.Input(in_2), .Output(complemento_a_2_2_output));
  Multiplexer #(.width(32)) multiplexer_1 (
    .in0(in_1), .in1(complemento_a_2_1_output), .out(multiplexer_1_out), .sel(in_1[31]));  // open: en
  Multiplexer #(.width(32)) multiplexer_2 (
    .in0(in_2), .in1(complemento_a_2_2_output), .out(multiplexer_2_out), .sel(in_2[31]));  // open: en
  Divider #(.width(32)) divider_1 (
    .a(multiplexer_1_out), .b(multiplexer_2_out), .out(Output), .rem(Output_2));  // open: upper
endmodule

module Slt (
  input  [31:0] Rs,
  input  [31:0] Rt,
  output [31:0] Output
);

  wire comparator_1_lt;
  wire [0:0] not_16_out;
  wire [15:0] multiplexer_1_out;
  wire [15:1] not_1_out;

  not not_1 (not_1_out[1], 1'b1);
  not not_2 (not_1_out[2], 1'b1);
  not not_3 (not_1_out[3], 1'b1);
  not not_4 (not_1_out[4], 1'b1);
  not not_5 (not_1_out[5], 1'b1);
  not not_6 (not_1_out[6], 1'b1);
  not not_7 (not_1_out[7], 1'b1);
  not not_8 (not_1_out[8], 1'b1);
  not not_9 (not_1_out[9], 1'b1);
  not not_10 (not_1_out[10], 1'b1);
  not not_11 (not_1_out[11], 1'b1);
  not not_12 (not_1_out[12], 1'b1);
  not not_13 (not_1_out[13], 1'b1);
  not not_14 (not_1_out[14], 1'b1);
  not not_15 (not_1_out[15], 1'b1);
  Comparator #(.width(32)) comparator_1 (.a(Rs), .b(Rt), .lt(comparator_1_lt));  // open: gt, eq
  not not_16 (not_16_out[0], 1'b1);
  Multiplexer #(.width(16)) multiplexer_1 (
    .in0({not_1_out, not_16_out[0]}), .in1({not_1_out, 1'b1}), .out(multiplexer_1_out), .sel(comparator_1_lt));  // open: en
  assign Output = {{16{1'b0}}, multiplexer_1_out};  // Bit_Extender bit_extender_1
endmodule

module Slti (
  input  [31:0] Rs,
  input  [31:0] Constant,
  output [31:0] Output
);

  wire comparator_1_lt;
  wire [0:0] not_16_out;
  wire [15:0] multiplexer_1_out;
  wire [15:1] not_1_out;

  not not_1 (not_1_out[1], 1'b1);
  not not_2 (not_1_out[2], 1'b1);
  not not_3 (not_1_out[3], 1'b1);
  not not_4 (not_1_out[4], 1'b1);
  not not_5 (not_1_out[5], 1'b1);
  not not_6 (not_1_out[6], 1'b1);
  not not_7 (not_1_out[7], 1'b1);
  not not_8 (not_1_out[8], 1'b1);
  not not_9 (not_1_out[9], 1'b1);
  not not_10 (not_1_out[10], 1'b1);
  not not_11 (not_1_out[11], 1'b1);
  not not_12 (not_1_out[12], 1'b1);
  not not_13 (not_1_out[13], 1'b1);
  not not_14 (not_1_out[14], 1'b1);
  not not_15 (not_1_out[15], 1'b1);
  Comparator #(.width(32)) comparator_1 (.a(Rs), .b(Constant), .lt(comparator_1_lt));  // open: gt, eq
  not not_16 (not_16_out[0], 1'b1);
  Multiplexer #(.width(16)) multiplexer_1 (
    .in0({not_1_out, not_16_out[0]}), .in1({not_1_out, 1'b1}), .out(multiplexer_1_out), .sel(comparator_1_lt));  // open: en
  assign Output = {{16{1'b0}}, multiplexer_1_out};  // Bit_Extender bit_extender_1
endmodule

module Sltiu (
  input  [31:0] Rs,
  input  [31:0] Constant,
  output [31:0] Output
);

  wire comparator_1_lt;
  wire [0:0] not_16_out;
  wire [15:0] multiplexer_1_out;
  wire [15:1] not_1_out;

  not not_1 (not_1_out[1], 1'b1);
  not not_2 (not_1_out[2], 1'b1);
  not not_3 (not_1_out[3], 1'b1);
  not not_4 (not_1_out[4], 1'b1);
  not not_5 (not_1_out[5], 1'b1);
  not not_6 (not_1_out[6], 1'b1);
  not not_7 (not_1_out[7], 1'b1);
  not not_8 (not_1_out[8], 1'b1);
  not not_9 (not_1_out[9], 1'b1);
  not not_10 (not_1_out[10], 1'b1);
  not not_11 (not_1_out[11], 1'b1);
  not not_12 (not_1_out[12], 1'b1);
  not not_13 (not_1_out[13], 1'b1);
  not not_14 (not_1_out[14], 1'b1);
  not not_15 (not_1_out[15], 1'b1);
  Comparator #(.width(32)) comparator_1 (.a(Rs), .b(Constant), .lt(comparator_1_lt));  // open: gt, eq
  not not_16 (not_16_out[0], 1'b1);
  Multiplexer #(.width(16)) multiplexer_1 (
    .in0({not_1_out, not_16_out[0]}), .in1({not_1_out, 1'b1}), .out(multiplexer_1_out), .sel(comparator_1_lt));  // open: en
  assign Output = {{16{1'b0}}, multiplexer_1_out};  // Bit_Extender bit_extender_1
endmodule

// U / Slt
module Unsigned_Slt (
  input  [31:0] Rs,
  input  [31:0] Rt,
  output [31:0] Output
);

  wire comparator_1_lt;
  wire [0:0] not_16_out;
  wire [15:0] multiplexer_1_out;
  wire [15:1] not_1_out;

  not not_1 (not_1_out[1], 1'b1);
  not not_2 (not_1_out[2], 1'b1);
  not not_3 (not_1_out[3], 1'b1);
  not not_4 (not_1_out[4], 1'b1);
  not not_5 (not_1_out[5], 1'b1);
  not not_6 (not_1_out[6], 1'b1);
  not not_7 (not_1_out[7], 1'b1);
  not not_8 (not_1_out[8], 1'b1);
  not not_9 (not_1_out[9], 1'b1);
  not not_10 (not_1_out[10], 1'b1);
  not not_11 (not_1_out[11], 1'b1);
  not not_12 (not_1_out[12], 1'b1);
  not not_13 (not_1_out[13], 1'b1);
  not not_14 (not_1_out[14], 1'b1);
  not not_15 (not_1_out[15], 1'b1);
  Comparator #(.width(32), .mode("unsigned")) comparator_1 (.a(Rs), .b(Rt), .lt(comparator_1_lt));  // open: gt, eq
  not not_16 (not_16_out[0], 1'b1);
  Multiplexer #(.width(16)) multiplexer_1 (
    .in0({not_1_out, not_16_out[0]}), .in1({not_1_out, 1'b1}), .out(multiplexer_1_out), .sel(comparator_1_lt));  // open: en
  assign Output = {{16{1'b0}}, multiplexer_1_out};  // Bit_Extender bit_extender_1
endmodule

module Complemento_a_2 (
  input  [31:0] Input,
  output [31:0] Output
);

  wire [31:0] bit_extender_1_out, not_1_out;

  assign not_1_out = ~Input;  // NOT_Gate not_1, 32 bits wide
  assign bit_extender_1_out = {{31{1'b0}}, 1'b1};  // Bit_Extender bit_extender_1
  // Probe on bit_extender_1_out
  Adder #(.width(32)) adder_1 (.a(not_1_out), .b(bit_extender_1_out), .out(Output));  // open: cin, cout
endmodule

// Nop
module nop (
  input  [31:0] in_1,
  output Output
);

  wire or_1_out;

  or or_1 (or_1_out, in_1[0], in_1[1], in_1[2], in_1[3], in_1[4], in_1[5], in_1[6], in_1[7], in_1[8], in_1[9], in_1[10], in_1[11], in_1[12], in_1[13], in_1[14], in_1[15], in_1[17], in_1[18], in_1[19], in_1[20], in_1[21], in_1[22], in_1[23], in_1[24], in_1[25], in_1[26], in_1[27], in_1[28], in_1[29], in_1[30], in_1[31], in_1[16]);
  not not_1 (Output, or_1_out);
endmodule

module Beq (
  input  [31:0] A,
  input  [31:0] B,
  input  [31:0] PC,
  input  [15:0] Js,
  output [31:0] PC_prime
);

  wire comparator_1_eq;
  wire [2:2] not_1_out;
  wire [31:0] _4, adder_1_out, bit_extender_1_out, S1, S2;

  assign {_4[31:3], not_1_out[2], _4[1:0]} = ~{32{1'b1}};  // NOT_Gate not_1, 32 bits wide
  assign bit_extender_1_out = {{16{1'b0}}, Js};  // Bit_Extender bit_extender_1
  not not_2 (_4[2], not_1_out[2]);
  Comparator #(.width(32)) comparator_1 (.a(A), .b(B), .eq(comparator_1_eq));  // open: gt, lt
  Adder #(.width(32)) adder_1 (.a(PC), .b(bit_extender_1_out), .out(adder_1_out));  // open: cin, cout
  Multiplexer #(.width(32)) multiplexer_1 (.in0(S1), .in1(S2), .out(PC_prime), .sel(comparator_1_eq));  // open: en
  Adder #(.width(32)) adder_2 (.a(PC), .b(_4), .out(S1));  // open: cin, cout
  Adder #(.width(32)) adder_3 (.a(adder_1_out), .b(_4), .out(S2));  // open: cin, cout
endmodule

module Bne (
  input  [15:0] A,
  input  [15:0] B,
  input  [15:0] PC,
  input  [15:0] Js,
  output [15:0] PC_prime
);

  wire comparator_1_eq;
  wire [2:2] not_1_out;
  wire [15:0] _4, adder_1_out, S1, S2;

  assign {_4[15:3], not_1_out[2], _4[1:0]} = ~{16{1'b1}};  // NOT_Gate not_1, 16 bits wide
  not not_2 (_4[2], not_1_out[2]);
  Comparator #(.width(16)) comparator_1 (.a(A), .b(B), .eq(comparator_1_eq));  // open: gt, lt
  Adder #(.width(16)) adder_1 (.a(PC), .b(Js), .out(adder_1_out));  // open: cin, cout
  Multiplexer #(.width(16)) multiplexer_1 (.in0(S1), .in1(S2), .out(PC_prime), .sel(comparator_1_eq));  // open: en
  Adder #(.width(16)) adder_2 (.a(PC), .b(_4), .out(S2));  // open: cin, cout
  Adder #(.width(16)) adder_3 (.a(adder_1_out), .b(_4), .out(S1));  // open: cin, cout
endmodule

module Blez (
  input  [15:0] A,
  input  [15:0] PC,
  input  [15:0] Js,
  output [15:0] PC_prime
);

  wire comparator_1_eq, comparator_1_lt, or_1_out;
  wire [2:2] not_1_out;
  wire [15:0] _0, _4, adder_1_out, S1, S2;

  assign {_4[15:3], not_1_out[2], _4[1:0]} = ~{16{1'b1}};  // NOT_Gate not_1, 16 bits wide
  assign _0 = ~{16{1'b1}};  // NOT_Gate not_2, 16 bits wide
  not not_3 (_4[2], not_1_out[2]);
  Comparator #(.width(16)) comparator_1 (.a(A), .b(_0), .eq(comparator_1_eq), .lt(comparator_1_lt));  // open: gt
  Adder #(.width(16)) adder_1 (.a(PC), .b(Js), .out(adder_1_out));  // open: cin, cout
  Multiplexer #(.width(16)) multiplexer_1 (.in0(S1), .in1(S2), .out(PC_prime), .sel(or_1_out));  // open: en
  or or_1 (or_1_out, comparator_1_eq, comparator_1_lt);
  Adder #(.width(16)) adder_2 (.a(PC), .b(_4), .out(S1));  // open: cin, cout
  Adder #(.width(16)) adder_3 (.a(adder_1_out), .b(_4), .out(S2));  // open: cin, cout
endmodule

module Bgtz (
  input  [15:0] A,
  input  [15:0] PC,
  input  [15:0] Js,
  output [15:0] PC_prime
);

  wire comparator_1_eq, comparator_1_lt, or_1_out;
  wire [2:2] not_1_out;
  wire [15:0] _0, _4, adder_1_out, S1, S2;

  assign {_4[15:3], not_1_out[2], _4[1:0]} = ~{16{1'b1}};  // NOT_Gate not_1, 16 bits wide
  assign _0 = ~{16{1'b1}};  // NOT_Gate not_2, 16 bits wide
  not not_3 (_4[2], not_1_out[2]);
  Comparator #(.width(16)) comparator_1 (.a(A), .b(_0), .eq(comparator_1_eq), .lt(comparator_1_lt));  // open: gt
  Adder #(.width(16)) adder_1 (.a(PC), .b(Js), .out(adder_1_out));  // open: cin, cout
  Multiplexer #(.width(16)) multiplexer_1 (.in0(S1), .in1(S2), .out(PC_prime), .sel(or_1_out));  // open: en
  or or_1 (or_1_out, comparator_1_eq, comparator_1_lt);
  Adder #(.width(16)) adder_2 (.a(PC), .b(_4), .out(S2));  // open: cin, cout
  Adder #(.width(16)) adder_3 (.a(adder_1_out), .b(_4), .out(S1));  // open: cin, cout
endmodule

module Bltz (
  input  [15:0] A,
  input  [15:0] PC,
  input  [15:0] Js,
  output [15:0] PC_prime
);

  wire comparator_1_lt;
  wire [2:2] not_1_out;
  wire [15:0] _0, _4, adder_1_out, S1, S2;

  assign {_4[15:3], not_1_out[2], _4[1:0]} = ~{16{1'b1}};  // NOT_Gate not_1, 16 bits wide
  assign _0 = ~{16{1'b1}};  // NOT_Gate not_2, 16 bits wide
  not not_3 (_4[2], not_1_out[2]);
  Comparator #(.width(16)) comparator_1 (.a(A), .b(_0), .lt(comparator_1_lt));  // open: gt, eq
  Adder #(.width(16)) adder_1 (.a(PC), .b(Js), .out(adder_1_out));  // open: cin, cout
  Multiplexer #(.width(16)) multiplexer_1 (.in0(S1), .in1(S2), .out(PC_prime), .sel(comparator_1_lt));  // open: en
  Adder #(.width(16)) adder_2 (.a(PC), .b(_4), .out(S1));  // open: cin, cout
  Adder #(.width(16)) adder_3 (.a(adder_1_out), .b(_4), .out(S2));  // open: cin, cout
endmodule

module Jr (
  input  [15:0] A,
  output [15:0] PC_prime
);


  assign PC_prime = A;
endmodule
